// Logisim project tHE FULL ADDER.circ as structural Verilog: 1 circuit, main circuit main
module main (
  input  A,
  input  B,
  input  C,
  input  COUT,
  output SUM
);

  wire and_1_out, and_2_out, or_1_out, xor_1_out, xor_2_out;

  and and_1 (and_1_out, B, A);
  xor xor_1 (xor_1_out, A, B);
  xor xor_2 (xor_2_out, xor_1_out, C);
  and and_2 (and_2_out, xor_1_out, C);
  or or_1 (or_1_out, and_1_out, and_2_out);
endmodule
